# Fritzing sketch ReedSensor-v3 (saved by Fritzing 0.9.2b)
circuit board: 1.81723cm x 3.12479cm
breadboards: 1

parts:
  Reed = Reed switch [package=THT]
  Attiny85 = attiny85 [package=dip]
  JP1 = Header 3 [package=screwterminal-3.5mm-3_lock.007s]
  SW3 = DIP SWITCH [package=dipswitch-02]
  SW2 = DIP SWITCH [package=dipswitch-02]
  12kOhm = Resistor [tolerance=±1% resistance=12k package="0805 [SMD]"]
  20kOhm = Resistor [tolerance=±1% resistance=20k package="0805 [SMD]"]
  39kOhm = Resistor [tolerance=±1% resistance=39k package="0805 [SMD]"]
  68kOhm = Resistor [tolerance=±1% resistance=68k package="0805 [SMD]"]
  LED1 = smd LED [color="Red (633nm)" package="0805 [SMD]"]
  100nF = Ceramic Capacitor [capacitance=100nF package="0805 [SMD, multilayer]"]
  6_8kOhm = Resistor [tolerance=±1% resistance=6.8k package="0805 [SMD]"]
  JP2 = Header 1 [package=1x01_offset]
  JP3 = Header 1 [package=1x01_offset]

nets:
  N1: Reed.pin_1, Attiny85.Pin_6
  N2: Reed.pin_2, Attiny85.Pin_4, JP1.3, 12kOhm.Pin_1, 20kOhm.Pin_1, 39kOhm.Pin_1, 68kOhm.Pin_1, LED1.cathode, 100nF.1, JP3.1
  N3: Attiny85.Pin_2, SW3.3, SW3.4, SW2.3, SW2.4, 100nF.0, 6_8kOhm.Pin_1
  N4: Attiny85.Pin_3, LED1.anode
  N5: Attiny85.Pin_5, JP1.1
  N6: Attiny85.Pin_8, JP1.2, 6_8kOhm.Pin_0, JP2.1
  N7: SW3.1, 12kOhm.Pin_0
  N8: SW3.2, 20kOhm.Pin_0
  N9: SW2.1, 39kOhm.Pin_0
  N10: SW2.2, 68kOhm.Pin_0
