# Fritzing sketch ReedSensor (saved by Fritzing 0.9.2b)
circuit board: 2.4001cm x 3.95904cm
breadboards: 1

parts:
  Reed = Reed switch [package=THT]
  Attiny85 = attiny85 [package=dip]
  JP1 = Header 3 [package=screwterminal-3.5mm-3_lock.007s]
  39kOhm = Resistor [tolerance=±1% resistance=68k package=THT]
  68kOhm = Resistor [tolerance=±1% resistance=39k package=THT]
  12kOhm = Resistor [tolerance=±1% resistance=20k package=THT]
  20kOhm = Resistor [tolerance=±1% resistance=12k package=THT]
  SW3 = DIP SWITCH [package=dipswitch-02]
  SW2 = DIP SWITCH [package=dipswitch-02]
  BAT1 = Battery Holders [package=battcom_20mm_pth]
  6_8kOhm = Resistor [tolerance=±1% resistance=6.8k package=THT]
  100nF = Ceramic Capacitor [capacitance=100nF package="200 mil [THT, multilayer]"]
  LED1 = LED - 3mm [color="Red (633nm)" package="3 mm [THT]"]

nets:
  N1: Reed.pin_1, Attiny85.Pin_6
  N2: Reed.pin_2, Attiny85.Pin_4, JP1.3, 39kOhm.Pin_1, 68kOhm.Pin_1, 12kOhm.Pin_1, 20kOhm.Pin_1, BAT1.-, 100nF.1, LED1.cathode
  N3: Attiny85.Pin_2, SW3.3, SW3.4, SW2.3, SW2.4, 6_8kOhm.Pin_1, 100nF.0
  N4: Attiny85.Pin_3, LED1.anode
  N5: Attiny85.Pin_5, JP1.1
  N6: Attiny85.Pin_8, JP1.2, BAT1.+, 6_8kOhm.Pin_0
  N7: 39kOhm.Pin_0, SW2.1
  N8: 68kOhm.Pin_0, SW2.2
  N9: 12kOhm.Pin_0, SW3.1
  N10: 20kOhm.Pin_0, SW3.2
