# Fritzing sketch TemperatureSensor (saved by Fritzing 0.9.2b)
circuit board: 1.58033cm x 2.09489cm
breadboards: 1

parts:
  U1 = attiny85 [package=dip]
  DHT1 = DHT11 Humitidy and Temperature Sensor
  JP1 = Header 3 [package=molex-1x3_lock]
  JP2 = Header 1 [package=1x01_offset]
  JP3 = Header 1 [package=1x01_offset]
  LED1 = smd LED [color="Red (633nm)" package="0603 [SMD]"]

nets:
  N1: U1.Pin_4, DHT1.GND, JP1.1, JP2.1, LED1.anode
  N2: U1.Pin_5, JP1.3
  N3: U1.Pin_6, DHT1.DATA, DHT1.NULL
  N4: U1.Pin_8, DHT1.VDD, JP1.2, JP3.1, LED1.cathode

custom parts:
  DHT11 Humitidy and Temperature Sensor: DHT11 Humidity and Temperature Sensor
